// Logisim project Game.circ as structural Verilog: 1 circuit, main circuit main
module main (
  input  in_1,
  input  reset,
  input  \wł_wył ,
  input  in_4,
  input  [6:0] in_5,
  output [15:0] out_6,
  output [15:0] out_7,
  output [15:0] out_8,
  output [15:0] out_9,
  output [15:0] out_10,
  output [15:0] out_11,
  output [15:0] out_12,
  output [15:0] out_13,
  output [15:0] out_14,
  output [15:0] out_15,
  output [15:0] out_16,
  output [15:0] out_17,
  output [15:0] out_18,
  output [15:0] out_19,
  output [15:0] out_20,
  output [15:0] out_21,
  output [15:0] out_22,
  output [15:0] out_23,
  output [15:0] out_24,
  output [15:0] out_25,
  output [3:0] out_26,
  output [3:0] out_27,
  output [3:0] out_28,
  output [15:0] out_29,
  output [3:0] out_30,
  output [15:0] out_31,
  output [15:0] out_32,
  output [15:0] out_33,
  output [15:0] out_34,
  output [15:0] out_35,
  output [15:0] out_36,
  output [15:0] out_37,
  output [15:0] out_38,
  output [3:0] out_39,
  output [3:0] out_40,
  output [15:0] out_41,
  output [3:0] out_42,
  output [3:0] out_43,
  output [15:0] out_44,
  output [15:0] out_45,
  output [15:0] out_46
);

  wire and_1_out, and_2_out, clock_1_out, comparator_1_gt, comparator_2_eq, comparator_2_lt, comparator_3_gt,
       controlled_buffer_2_out, counter_1_q, counter_2_carry, counter_3_carry, counter_5_carry,
       counter_6_carry, counter_7_carry, d_ff_1_q, d_ff_1_qn, main_1_out_6, main_2_out_7, main_2_out_15,
       not_1_out, not_2_out, not_3_out, or_1_out, pull_resistor_1_node, pull_resistor_4_node,
       pull_resistor_7_node;
  wire [0:0] random_1_out, shifter_2_out;
  wire [3:0] counter_7_q, random_2_out;
  wire [6:0] controlled_buffer_3_out;
  wire [7:0] counter_2_q;
  wire [14:0] pull_resistor_2_node;
  wire [15:0] and_3_out, and_4_out, and_5_out, and_6_out, main_1_out_2, main_1_out_3, main_1_out_4,
       main_1_out_5, main_2_out_37, main_2_out_38, main_2_out_39, main_2_out_40, multiplexer_2_out, or_2_out,
       pull_resistor_3_node, pull_resistor_6_node, pull_resistor_8_node, register_1_q, register_2_q,
       rom_1_data, shifter_1_out;

  Counter #(.width(1), .max('h1)) counter_1 (
    .Q(counter_1_q), .clk(and_1_out), .clr(reset));  // open: load, D, count, carry
  and and_1 (and_1_out, counter_7_carry, counter_2_carry);
  not not_1 (not_1_out, counter_7_carry);
  Pull_Resistor pull_resistor_1 (.node(pull_resistor_1_node));
  and and_2 (and_2_out, pull_resistor_1_node, d_ff_1_qn);
  assign pull_resistor_1_node = not_2_out ? \wł_wył  : 1'bz;  // Controlled_Buffer controlled_buffer_1
  not not_2 (not_2_out, counter_1_q);
  Register #(.width(16)) register_1 (
    .D({out_26, out_27, out_28, out_30}), .Q(register_1_q), .clk(counter_7_carry));  // open: en, clr
  Register #(.width(16)) register_2 (
    .D({out_43, out_42, out_40, out_39}), .Q(register_2_q), .clk(not_1_out));  // open: en, clr
  Counter counter_2 (
    .count(and_2_out), .Q(counter_2_q), .carry(counter_2_carry), .clk(in_1), .clr(reset));  // open: load, D
  or or_1 (or_1_out, reset, counter_2_carry);
  Pull_Resistor pull_resistor_2 (.node(pull_resistor_2_node));
  Random #(.width(1)) random_1 (.clk(in_1), .out(random_1_out[0]));  // open: next, clr
  Counter #(.width(4), .max('h9)) counter_3 (
    .Q(out_27), .carry(counter_3_carry), .clk(counter_5_carry), .clr(or_1_out));  // open: load, D, count
  Counter #(.width(4), .max('h9)) counter_4 (
    .Q(out_26), .clk(counter_3_carry), .clr(or_1_out));  // open: load, D, count, carry
  assign controlled_buffer_2_out = \wł_wył  ? in_1 : 1'bz;  // Controlled_Buffer controlled_buffer_2
  Comparator #(.width(16)) comparator_1 (.a(register_2_q), .b(register_1_q), .gt(comparator_1_gt));  // open: eq, lt
  D_Flip_Flop d_ff_1 (
    .clk(comparator_2_eq), .D(comparator_2_eq), .Q(d_ff_1_q), .Qn(d_ff_1_qn), .reset(counter_7_carry));  // open: preset, en
  Counter #(.width(4), .max('h9)) counter_5 (
    .Q(out_28), .carry(counter_5_carry), .clk(counter_6_carry), .clr(or_1_out));  // open: load, D, count
  Multiplexer #(.width(16), .enable("false")) multiplexer_1 (
    .in0(register_1_q), .in1(register_2_q), .out({out_43, out_42, out_40, out_39}), .sel(comparator_1_gt));
  ROM #(.dataWidth(16)) rom_1 (.addr(counter_2_q), .data(rom_1_data));  // open: sel
  Pull_Resistor #(.pull(1)) pull_resistor_3 (.node(pull_resistor_3_node));
  Counter #(.width(4), .max('h9)) counter_6 (
    .count(d_ff_1_q), .Q(out_30), .carry(counter_6_carry), .clk(controlled_buffer_2_out), .clr(or_1_out));  // open: load, D
  Comparator #(.width(16)) comparator_2 (
    .a(rom_1_data), .b(pull_resistor_3_node), .eq(comparator_2_eq), .lt(comparator_2_lt));  // open: gt
  Random #(.width(4)) random_2 (.clk(in_1), .next(d_ff_1_q), .out(random_2_out));  // open: clr
  Shifter #(.width(16)) shifter_1 (
    .in({pull_resistor_2_node, random_1_out[0]}), .\dist (random_2_out), .out(shifter_1_out));
  Pull_Resistor pull_resistor_4 (.node(pull_resistor_4_node));
  assign controlled_buffer_3_out = d_ff_1_q ? in_5 : 7'bz;  // Controlled_Buffer controlled_buffer_3
  Pull_Resistor pull_resistor_5 (.node(controlled_buffer_3_out));
  Multiplexer #(.width(16)) multiplexer_2 (
    .in0(rom_1_data), .in1(shifter_1_out), .out(multiplexer_2_out), .sel(d_ff_1_q));  // open: en
  Pull_Resistor #(.pull(1)) pull_resistor_6 (.node(pull_resistor_6_node));
  Counter #(.width(4), .max('hf)) counter_7 (
    .count(d_ff_1_q), .Q(counter_7_q), .carry(counter_7_carry), .clk(pull_resistor_4_node), .clr(or_1_out));  // open: load, D
  assign pull_resistor_4_node = not_3_out ? comparator_3_gt : 1'bz;  // Controlled_Buffer controlled_buffer_4
  not not_3 (not_3_out, in_4);
  Clock #(.highDuration(2), .lowDuration(2)) clock_1 (.out(clock_1_out));
  Pull_Resistor pull_resistor_7 (.node(pull_resistor_7_node));
  assign pull_resistor_7_node = clock_1_out ? main_1_out_6 : 1'bz;  // Controlled_Buffer controlled_buffer_5
  Shifter #(.width(16), .shift("lr")) shifter_2 (
    .in(pull_resistor_6_node), .\dist (counter_7_q), .out({out_6[15:1], shifter_2_out[0]}));
  assign or_2_out = and_3_out | and_4_out | and_5_out | and_6_out;  // OR_Gate or_2, 16 bits wide
  Comparator #(.width(16)) comparator_3 (.a(or_2_out), .b(pull_resistor_8_node), .gt(comparator_3_gt));  // open: eq, lt
  Pull_Resistor pull_resistor_8 (.node(pull_resistor_8_node));
  Sterowanie_main main_1 (
    .in_1(controlled_buffer_3_out), .out_2(main_1_out_2), .out_3(main_1_out_3), .out_4(main_1_out_4),
    .out_5(main_1_out_5), .out_6(main_1_out_6));
  ekran_main main_2 (
    .in_1(main_1_out_2), .in_2(pull_resistor_7_node), .out_8(out_38), .out_9(out_37), .out_10(out_36),
    .out_11(out_35), .out_12(out_34), .out_13(out_33), .out_14(out_32), .out_16(out_31), .out_17(out_29),
    .out_18(out_25), .out_19(out_24), .out_20(out_23), .out_21(out_22), .out_22(out_21), .out_23(out_20),
    .out_24(out_19), .out_25(out_18), .out_26(out_17), .out_27(out_16), .out_28(out_15), .out_29(out_14),
    .out_30(out_13), .out_31(out_12), .out_32(out_11), .out_33(out_10), .out_34(out_9), .out_35(out_8),
    .out_37(main_2_out_37), .in_4(multiplexer_2_out), .in_3(\wł_wył ), .out_38(main_2_out_38),
    .out_39(main_2_out_39), .out_40(main_2_out_40), .in_5(reset), .out_15(main_2_out_15), .in_6(in_1),
    .out_36(out_7), .out_7(main_2_out_7));
  assign and_3_out = main_2_out_40 & main_1_out_2;  // AND_Gate and_3, 16 bits wide
  assign and_4_out = main_2_out_39 & main_1_out_3;  // AND_Gate and_4, 16 bits wide
  assign and_5_out = main_2_out_38 & main_1_out_4;  // AND_Gate and_5, 16 bits wide
  assign and_6_out = main_2_out_37 & main_1_out_5;  // AND_Gate and_6, 16 bits wide
  assign out_41 = main_2_out_40 | main_1_out_2;  // OR_Gate or_3, 16 bits wide
  assign out_44 = main_2_out_39 | main_1_out_3;  // OR_Gate or_4, 16 bits wide
  assign out_45 = main_2_out_38 | main_1_out_4;  // OR_Gate or_5, 16 bits wide
  assign out_46 = main_2_out_37 | main_1_out_5;  // OR_Gate or_6, 16 bits wide

  assign out_6[0] = out_6[1];

  // Notes on the sheet:
  //   contents of rom_1 (hex, n*v repeats v):
  //   ea48 2a48 ee4e 8a4a ea4e 0 ee0 880 8e0 880 ee0 0 3a14 a14 3b9c 2294 3b9c 36*0 ffff 0 0 4475 aa45
  //   aa76 aa45 4a76 0 0 d517 b514 9d17 9554 48a7 0 0 ffff
  //   Kolizja asteroida/pocisk
endmodule
