// Logisim project Projekt_tc.circ as structural Verilog: 1 circuit, main circuit main
module main (
  input  in_1,
  input  in_2
);

  wire button_1_out, clock_1_out;
  wire [3:0] main_1_out_26, main_1_out_27, main_1_out_28, main_1_out_30, main_1_out_39, main_1_out_40,
       main_1_out_42, main_1_out_43;
  wire [6:0] keyboard_1_data;
  wire [15:0] main_1_out_6, main_1_out_7, main_1_out_8, main_1_out_9, main_1_out_10, main_1_out_11,
       main_1_out_12, main_1_out_13, main_1_out_14, main_1_out_15, main_1_out_16, main_1_out_17,
       main_1_out_18, main_1_out_19, main_1_out_20, main_1_out_21, main_1_out_22, main_1_out_23,
       main_1_out_24, main_1_out_25, main_1_out_29, main_1_out_31, main_1_out_32, main_1_out_33,
       main_1_out_34, main_1_out_35, main_1_out_36, main_1_out_37, main_1_out_38, main_1_out_41,
       main_1_out_44, main_1_out_45, main_1_out_46;

  Hex_Digit_Display hex_digit_display_1 (.value(main_1_out_43));  // open: dp
  Game_main main_1 (
    .in_5(keyboard_1_data), .out_6(main_1_out_6), .out_7(main_1_out_7), .out_8(main_1_out_8),
    .\wł_wył (in_2), .out_9(main_1_out_9), .out_10(main_1_out_10), .out_11(main_1_out_11),
    .out_12(main_1_out_12), .out_13(main_1_out_13), .out_14(main_1_out_14), .out_15(main_1_out_15),
    .out_16(main_1_out_16), .out_17(main_1_out_17), .out_18(main_1_out_18), .out_19(main_1_out_19),
    .out_20(main_1_out_20), .out_21(main_1_out_21), .out_22(main_1_out_22), .out_23(main_1_out_23),
    .out_24(main_1_out_24), .out_25(main_1_out_25), .out_29(main_1_out_29), .out_26(main_1_out_26),
    .out_27(main_1_out_27), .out_28(main_1_out_28), .out_30(main_1_out_30), .out_31(main_1_out_31),
    .out_32(main_1_out_32), .out_33(main_1_out_33), .out_34(main_1_out_34), .out_35(main_1_out_35),
    .out_36(main_1_out_36), .out_37(main_1_out_37), .out_38(main_1_out_38), .out_41(main_1_out_41),
    .out_44(main_1_out_44), .out_45(main_1_out_45), .out_46(main_1_out_46), .in_1(clock_1_out),
    .reset(button_1_out), .in_4(in_1), .out_39(main_1_out_39), .out_42(main_1_out_42),
    .out_40(main_1_out_40), .out_43(main_1_out_43));
  Clock clock_1 (.out(clock_1_out));
  Hex_Digit_Display hex_digit_display_2 (.value(main_1_out_42));  // open: dp
  Hex_Digit_Display hex_digit_display_3 (.value(main_1_out_40));  // open: dp
  Button W ();  // open: out
  Button A ();  // open: out
  Button D ();  // open: out
  Button S ();  // open: out
  Button button_1 (.out(button_1_out));
  Hex_Digit_Display hex_digit_display_4 (.value(main_1_out_26));  // open: dp
  Hex_Digit_Display hex_digit_display_5 (.value(main_1_out_39));  // open: dp
  DotMatrix #(.inputtype("row"), .matrixcols(16), .matrixrows(1)) dotmatrix_1 (.row0(main_1_out_6));
  DotMatrix #(.inputtype("row"), .matrixcols(16), .matrixrows(32)) dotmatrix_2 (
    .row0(main_1_out_7), .row1(main_1_out_8), .row2(main_1_out_9), .row3(main_1_out_10),
    .row4(main_1_out_11), .row5(main_1_out_12), .row6(main_1_out_13), .row7(main_1_out_14),
    .row8(main_1_out_15), .row9(main_1_out_16), .row10(main_1_out_17), .row11(main_1_out_18),
    .row12(main_1_out_19), .row13(main_1_out_20), .row14(main_1_out_21), .row15(main_1_out_22),
    .row16(main_1_out_23), .row17(main_1_out_24), .row18(main_1_out_25), .row19(main_1_out_29),
    .row20(main_1_out_31), .row21(main_1_out_32), .row22(main_1_out_33), .row23(main_1_out_34),
    .row24(main_1_out_35), .row25(main_1_out_36), .row26(main_1_out_37), .row27(main_1_out_38),
    .row28(main_1_out_41), .row29(main_1_out_44), .row30(main_1_out_45), .row31(main_1_out_46));
  Keyboard #(.buflen(1)) keyboard_1 (.clk(clock_1_out), .data(keyboard_1_data));  // open: re, clr, avail
  Hex_Digit_Display hex_digit_display_6 (.value(main_1_out_28));  // open: dp
  Hex_Digit_Display hex_digit_display_7 (.value(main_1_out_27));  // open: dp
  Hex_Digit_Display hex_digit_display_8 (.value(main_1_out_30));  // open: dp

  // Notes on the sheet:
  //   freq 32/16 Hz
  //   Highest score
  //   Sterowanie A,D
  //   Strzał W
endmodule
