// Logisim project Sterowanie.circ as structural Verilog: 1 circuit, main circuit main
module main (
  input  [6:0] in_1,
  output [15:0] out_2,
  output [15:0] out_3,
  output [15:0] out_4,
  output [15:0] out_5,
  output out_6
);

  wire clock_1_out, comparator_1_eq, comparator_2_eq, or_1_out;
  wire [4:0] counter_1_q;

  Comparator #(.width(7)) comparator_1 (.a(in_1), .b(7'b1100100), .eq(comparator_1_eq));  // open: gt, lt
  Comparator #(.width(7)) comparator_2 (.a(in_1), .b(7'b1100001), .eq(comparator_2_eq));  // open: gt, lt
  Comparator #(.width(7)) comparator_3 (.a(in_1), .b(7'b1110111), .eq(out_6));  // open: gt, lt
  or or_1 (or_1_out, comparator_1_eq, comparator_2_eq);
  Shifter #(.width(32), .shift("lr")) shifter_1 (.in(32'he0004000), .\dist (counter_1_q), .out({out_3, out_2}));
  Shifter #(.width(32), .shift("lr")) shifter_2 (.in(32'ha0004000), .\dist (counter_1_q), .out({out_5, out_4}));
  Counter #(.width(5), .max('hd)) counter_1 (
    .load(comparator_2_eq), .count(or_1_out), .Q(counter_1_q), .clk(clock_1_out));  // open: D, carry, clr
  Clock clock_1 (.out(clock_1_out));
endmodule
