// Logisim project ekran.circ as structural Verilog: 1 circuit, main circuit main
module main (
  input  [15:0] in_1,
  input  in_2,
  input  in_3,
  input  [15:0] in_4,
  input  in_5,
  input  in_6,
  output out_7,
  output [15:0] out_8,
  output [15:0] out_9,
  output [15:0] out_10,
  output [15:0] out_11,
  output [15:0] out_12,
  output [15:0] out_13,
  output [15:0] out_14,
  output out_15,
  output [15:0] out_16,
  output [15:0] out_17,
  output [15:0] out_18,
  output [15:0] out_19,
  output [15:0] out_20,
  output [15:0] out_21,
  output [15:0] out_22,
  output [15:0] out_23,
  output [15:0] out_24,
  output [15:0] out_25,
  output [15:0] out_26,
  output [15:0] out_27,
  output [15:0] out_28,
  output [15:0] out_29,
  output [15:0] out_30,
  output [15:0] out_31,
  output [15:0] out_32,
  output [15:0] out_33,
  output [15:0] out_34,
  output [15:0] out_35,
  output [15:0] out_36,
  output [15:0] out_37,
  output [15:0] out_38,
  output [15:0] out_39,
  output [15:0] out_40
);

  wire main_1_out_8, main_1_out_10, main_2_out_8, main_2_out_10, main_3_out_8, main_3_out_10, main_4_out_8,
       main_4_out_10, main_5_out_8, main_5_out_10, main_6_out_8, main_6_out_10, main_7_out_8, main_7_out_10,
       main_8_out_8, main_8_out_10, main_9_out_8, main_9_out_10, main_10_out_8, main_10_out_10,
       main_11_out_8, main_11_out_10, main_12_out_8, main_12_out_10, main_13_out_8, main_13_out_10,
       main_14_out_8, main_14_out_10, main_15_out_8, main_15_out_10, main_16_out_8, main_16_out_10,
       main_17_out_8, main_17_out_10, main_18_out_8, main_18_out_10, main_19_out_8, main_19_out_10,
       main_20_out_8, main_20_out_10, main_21_out_8, main_21_out_10, main_22_out_8, main_22_out_10,
       main_23_out_8, main_23_out_10, main_24_out_8, main_24_out_10, main_25_out_8, main_25_out_10,
       main_26_out_8, main_26_out_10, main_27_out_8, main_27_out_10, main_28_out_8, pull_resistor_4_node, s1,
       s2, s3, s4, s5, s6, s7, s8, s9, s10, s11, s12, s13, s14, s15, s16, s17, s18, s19, s20, s21, s22, s23,
       s24, s25, s26, s27, s28;
  wire [15:0] main_29_out_57, main_29_out_58, main_29_out_59, main_29_out_60, main_29_out_61, main_29_out_62,
       main_29_out_63, main_29_out_64, main_29_out_65, main_29_out_66, main_29_out_67, main_29_out_68,
       main_29_out_69, main_29_out_70, main_29_out_71, main_29_out_72, main_29_out_73, main_29_out_74,
       main_29_out_75, main_29_out_76, main_29_out_77, main_29_out_78, main_29_out_79, main_29_out_80,
       main_29_out_81, main_29_out_82, main_29_out_83, multiplexer_1_out, pull_resistor_1_node,
       pull_resistor_2_node, pull_resistor_3_node, shift_register_1_q0, shift_register_1_q1,
       shift_register_1_q2, shift_register_1_q3, shift_register_1_q4, shift_register_1_q5,
       shift_register_1_q6, shift_register_1_q7, shift_register_1_q8, shift_register_1_q9,
       shift_register_1_q10, shift_register_1_q11, shift_register_1_q12, shift_register_1_q13,
       shift_register_1_q14, shift_register_1_q15, shift_register_1_q16, shift_register_1_q17,
       shift_register_1_q18, shift_register_1_q19, shift_register_1_q20, shift_register_1_q21,
       shift_register_1_q22, shift_register_1_q23, shift_register_1_q24, shift_register_1_q25,
       shift_register_1_q26, shift_register_1_q27, shift_register_2_q0, shift_register_2_q1,
       shift_register_2_q2, shift_register_2_q3, shift_register_2_q4, shift_register_2_q5,
       shift_register_2_q6, shift_register_2_q7, shift_register_2_q8, shift_register_2_q9,
       shift_register_2_q10, shift_register_2_q11, shift_register_2_q12, shift_register_2_q13,
       shift_register_2_q14, shift_register_2_q15, shift_register_2_q16, shift_register_2_q17,
       shift_register_2_q18, shift_register_2_q19, shift_register_2_q20, shift_register_2_q21,
       shift_register_2_q22, shift_register_2_q23, shift_register_2_q24, shift_register_2_q25,
       shift_register_2_q26, shift_register_2_q27, w1, w2, w3, w4, w5, w6, w7, w8, w9, w10, w11, w12, w13,
       w14, w15, w16, w17, w18, w19, w20, w21, w22, w23, w24, w25, w26, w27, w28;

  Pull_Resistor pull_resistor_1 (.node(pull_resistor_1_node));
  Multiplexer #(.width(16), .disabled(0), .enable("false")) multiplexer_1 (
    .in0(pull_resistor_1_node), .in1(in_1), .out(multiplexer_1_out), .sel(in_2));
  Pull_Resistor pull_resistor_2 (.node(pull_resistor_2_node));
  Shift_Register #(.width(16), .length(32)) shift_register_1 (
    .shift(in_3), .in(in_4), .clk(in_6), .load(out_15), .clr(in_5), .d0(pull_resistor_2_node),
    .q0(shift_register_1_q0), .d1(w28), .q1(shift_register_1_q1), .d2(w27), .q2(shift_register_1_q2),
    .d3(w26), .q3(shift_register_1_q3), .d4(w25), .q4(shift_register_1_q4), .d5(w24),
    .q5(shift_register_1_q5), .d6(w23), .q6(shift_register_1_q6), .d7(w22), .q7(shift_register_1_q7),
    .d8(w21), .q8(shift_register_1_q8), .d9(w20), .q9(shift_register_1_q9), .d10(w19),
    .q10(shift_register_1_q10), .d11(w18), .q11(shift_register_1_q11), .d12(w17), .q12(shift_register_1_q12),
    .d13(w16), .q13(shift_register_1_q13), .d14(w15), .q14(shift_register_1_q14), .d15(w14),
    .q15(shift_register_1_q15), .d16(w13), .q16(shift_register_1_q16), .d17(w12), .q17(shift_register_1_q17),
    .d18(w11), .q18(shift_register_1_q18), .d19(w10), .q19(shift_register_1_q19), .d20(w9),
    .q20(shift_register_1_q20), .d21(w8), .q21(shift_register_1_q21), .d22(w7), .q22(shift_register_1_q22),
    .d23(w6), .q23(shift_register_1_q23), .d24(w5), .q24(shift_register_1_q24), .d25(w4),
    .q25(shift_register_1_q25), .d26(w3), .q26(shift_register_1_q26), .d27(w2), .q27(shift_register_1_q27),
    .d28(out_40), .q28(out_40), .d29(out_39), .q29(out_39), .d30(out_38), .q30(out_38), .d31(out_37),
    .q31(out_37));  // open: out
  Pull_Resistor pull_resistor_3 (.node(pull_resistor_3_node));
  Shift_Register #(.width(16), .length(28)) shift_register_2 (
    .shift(in_3), .in(multiplexer_1_out), .clk(in_6), .load(out_7), .clr(in_5), .d0(pull_resistor_3_node),
    .q0(shift_register_2_q0), .d1(main_29_out_57), .q1(shift_register_2_q1), .d2(main_29_out_58),
    .q2(shift_register_2_q2), .d3(main_29_out_59), .q3(shift_register_2_q3), .d4(main_29_out_60),
    .q4(shift_register_2_q4), .d5(main_29_out_61), .q5(shift_register_2_q5), .d6(main_29_out_62),
    .q6(shift_register_2_q6), .d7(main_29_out_63), .q7(shift_register_2_q7), .d8(main_29_out_64),
    .q8(shift_register_2_q8), .d9(main_29_out_65), .q9(shift_register_2_q9), .d10(main_29_out_66),
    .q10(shift_register_2_q10), .d11(main_29_out_67), .q11(shift_register_2_q11), .d12(main_29_out_68),
    .q12(shift_register_2_q12), .d13(main_29_out_69), .q13(shift_register_2_q13), .d14(main_29_out_70),
    .q14(shift_register_2_q14), .d15(main_29_out_71), .q15(shift_register_2_q15), .d16(main_29_out_72),
    .q16(shift_register_2_q16), .d17(main_29_out_73), .q17(shift_register_2_q17), .d18(main_29_out_74),
    .q18(shift_register_2_q18), .d19(main_29_out_75), .q19(shift_register_2_q19), .d20(main_29_out_76),
    .q20(shift_register_2_q20), .d21(main_29_out_77), .q21(shift_register_2_q21), .d22(main_29_out_78),
    .q22(shift_register_2_q22), .d23(main_29_out_79), .q23(shift_register_2_q23), .d24(main_29_out_80),
    .q24(shift_register_2_q24), .d25(main_29_out_81), .q25(shift_register_2_q25), .d26(main_29_out_82),
    .q26(shift_register_2_q26), .d27(main_29_out_83), .q27(shift_register_2_q27));  // open: out
  Pull_Resistor pull_resistor_4 (.node(pull_resistor_4_node));
  kolizja_main main_1 (
    .in_1(shift_register_1_q27), .in_2(shift_register_2_q0), .out_7(w1), .out_8(main_1_out_8), .out_6(out_8),
    .out_9(s1), .in_3(shift_register_2_q1), .out_10(main_1_out_10), .in_5(pull_resistor_4_node), .in_4(in_6));
  kolizja_main main_2 (
    .in_1(shift_register_1_q26), .in_2(shift_register_2_q1), .out_7(w2), .out_8(main_2_out_8), .out_6(out_9),
    .out_9(s2), .in_3(shift_register_2_q2), .out_10(main_2_out_10), .in_5(main_1_out_10), .in_4(in_6));
  kolizja_main main_3 (
    .in_1(shift_register_1_q25), .in_2(shift_register_2_q2), .out_7(w3), .out_8(main_3_out_8),
    .out_6(out_10), .out_9(s3), .in_3(shift_register_2_q3), .out_10(main_3_out_10), .in_5(main_2_out_10),
    .in_4(in_6));
  kolizja_main main_4 (
    .in_1(shift_register_1_q24), .in_2(shift_register_2_q3), .out_7(w4), .out_8(main_4_out_8),
    .out_6(out_11), .out_9(s4), .in_3(shift_register_2_q4), .out_10(main_4_out_10), .in_5(main_3_out_10),
    .in_4(in_6));
  kolizja_main main_5 (
    .in_1(shift_register_1_q23), .in_2(shift_register_2_q4), .out_7(w5), .out_8(main_5_out_8),
    .out_6(out_12), .out_9(s5), .in_3(shift_register_2_q5), .out_10(main_5_out_10), .in_5(main_4_out_10),
    .in_4(in_6));
  kolizja_main main_6 (
    .in_1(shift_register_1_q22), .in_2(shift_register_2_q5), .out_7(w6), .out_8(main_6_out_8),
    .out_6(out_13), .out_9(s6), .in_3(shift_register_2_q6), .out_10(main_6_out_10), .in_5(main_5_out_10),
    .in_4(in_6));
  kolizja_main main_7 (
    .in_1(shift_register_1_q21), .in_2(shift_register_2_q6), .out_7(w7), .out_8(main_7_out_8),
    .out_6(out_14), .out_9(s7), .in_3(shift_register_2_q7), .out_10(main_7_out_10), .in_5(main_6_out_10),
    .in_4(in_6));
  kolizja_main main_8 (
    .in_1(shift_register_1_q20), .in_2(shift_register_2_q7), .out_7(w8), .out_8(main_8_out_8),
    .out_6(out_16), .out_9(s8), .in_3(shift_register_2_q8), .out_10(main_8_out_10), .in_5(main_7_out_10),
    .in_4(in_6));
  kolizja_main main_9 (
    .in_1(shift_register_1_q19), .in_2(shift_register_2_q8), .out_7(w9), .out_8(main_9_out_8),
    .out_6(out_17), .out_9(s9), .in_3(shift_register_2_q9), .out_10(main_9_out_10), .in_5(main_8_out_10),
    .in_4(in_6));
  kolizja_main main_10 (
    .in_1(shift_register_1_q18), .in_2(shift_register_2_q9), .out_7(w10), .out_8(main_10_out_8),
    .out_6(out_18), .out_9(s10), .in_3(shift_register_2_q10), .out_10(main_10_out_10), .in_5(main_9_out_10),
    .in_4(in_6));
  kolizja_main main_11 (
    .in_1(shift_register_1_q17), .in_2(shift_register_2_q10), .out_7(w11), .out_8(main_11_out_8),
    .out_6(out_19), .out_9(s11), .in_3(shift_register_2_q11), .out_10(main_11_out_10), .in_5(main_10_out_10),
    .in_4(in_6));
  kolizja_main main_12 (
    .in_1(shift_register_1_q16), .in_2(shift_register_2_q11), .out_7(w12), .out_8(main_12_out_8),
    .out_6(out_20), .out_9(s12), .in_3(shift_register_2_q12), .out_10(main_12_out_10), .in_5(main_11_out_10),
    .in_4(in_6));
  kolizja_main main_13 (
    .in_1(shift_register_1_q15), .in_2(shift_register_2_q12), .out_7(w13), .out_8(main_13_out_8),
    .out_6(out_21), .out_9(s13), .in_3(shift_register_2_q13), .out_10(main_13_out_10), .in_5(main_12_out_10),
    .in_4(in_6));
  kolizja_main main_14 (
    .in_1(shift_register_1_q14), .in_2(shift_register_2_q13), .out_7(w14), .out_8(main_14_out_8),
    .out_6(out_22), .out_9(s14), .in_3(shift_register_2_q14), .out_10(main_14_out_10), .in_5(main_13_out_10),
    .in_4(in_6));
  kolizja_main main_15 (
    .in_1(shift_register_1_q13), .in_2(shift_register_2_q14), .out_7(w15), .out_8(main_15_out_8),
    .out_6(out_23), .out_9(s15), .in_3(shift_register_2_q15), .out_10(main_15_out_10), .in_5(main_14_out_10),
    .in_4(in_6));
  kolizja_main main_16 (
    .in_1(shift_register_1_q12), .in_2(shift_register_2_q15), .out_7(w16), .out_8(main_16_out_8),
    .out_6(out_24), .out_9(s16), .in_3(shift_register_2_q16), .out_10(main_16_out_10), .in_5(main_15_out_10),
    .in_4(in_6));
  kolizja_main main_17 (
    .in_1(shift_register_1_q11), .in_2(shift_register_2_q16), .out_7(w17), .out_8(main_17_out_8),
    .out_6(out_25), .out_9(s17), .in_3(shift_register_2_q17), .out_10(main_17_out_10), .in_5(main_16_out_10),
    .in_4(in_6));
  kolizja_main main_18 (
    .in_1(shift_register_1_q10), .in_2(shift_register_2_q17), .out_7(w18), .out_8(main_18_out_8),
    .out_6(out_26), .out_9(s18), .in_3(shift_register_2_q18), .out_10(main_18_out_10), .in_5(main_17_out_10),
    .in_4(in_6));
  kolizja_main main_19 (
    .in_1(shift_register_1_q9), .in_2(shift_register_2_q18), .out_7(w19), .out_8(main_19_out_8),
    .out_6(out_27), .out_9(s19), .in_3(shift_register_2_q19), .out_10(main_19_out_10), .in_5(main_18_out_10),
    .in_4(in_6));
  kolizja_main main_20 (
    .in_1(shift_register_1_q8), .in_2(shift_register_2_q19), .out_7(w20), .out_8(main_20_out_8),
    .out_6(out_28), .out_9(s20), .in_3(shift_register_2_q20), .out_10(main_20_out_10), .in_5(main_19_out_10),
    .in_4(in_6));
  kolizja_main main_21 (
    .in_1(shift_register_1_q7), .in_2(shift_register_2_q20), .out_7(w21), .out_8(main_21_out_8),
    .out_6(out_29), .out_9(s21), .in_3(shift_register_2_q21), .out_10(main_21_out_10), .in_5(main_20_out_10),
    .in_4(in_6));
  kolizja_main main_22 (
    .in_1(shift_register_1_q6), .in_2(shift_register_2_q21), .out_7(w22), .out_8(main_22_out_8),
    .out_6(out_30), .out_9(s22), .in_3(shift_register_2_q22), .out_10(main_22_out_10), .in_5(main_21_out_10),
    .in_4(in_6));
  kolizja_main main_23 (
    .in_1(shift_register_1_q5), .in_2(shift_register_2_q22), .out_7(w23), .out_8(main_23_out_8),
    .out_6(out_31), .out_9(s23), .in_3(shift_register_2_q23), .out_10(main_23_out_10), .in_5(main_22_out_10),
    .in_4(in_6));
  kolizja_main main_24 (
    .in_1(shift_register_1_q4), .in_2(shift_register_2_q23), .out_7(w24), .out_8(main_24_out_8),
    .out_6(out_32), .out_9(s24), .in_3(shift_register_2_q24), .out_10(main_24_out_10), .in_5(main_23_out_10),
    .in_4(in_6));
  kolizja_main main_25 (
    .in_1(shift_register_1_q3), .in_2(shift_register_2_q24), .out_7(w25), .out_8(main_25_out_8),
    .out_6(out_33), .out_9(s25), .in_3(shift_register_2_q25), .out_10(main_25_out_10), .in_5(main_24_out_10),
    .in_4(in_6));
  kolizja_main main_26 (
    .in_1(shift_register_1_q2), .in_2(shift_register_2_q25), .out_7(w26), .out_8(main_26_out_8),
    .out_6(out_34), .out_9(s26), .in_3(shift_register_2_q26), .out_10(main_26_out_10), .in_5(main_25_out_10),
    .in_4(in_6));
  kolizja_main main_27 (
    .in_1(shift_register_1_q1), .in_2(shift_register_2_q26), .out_7(w27), .out_8(main_27_out_8),
    .out_6(out_35), .out_9(s27), .in_3(shift_register_2_q27), .out_10(main_27_out_10), .in_5(main_26_out_10),
    .in_4(in_6));
  kolizja_main main_28 (
    .in_1(shift_register_1_q0), .in_2(shift_register_2_q27), .out_7(w28), .out_8(main_28_out_8),
    .out_6(out_36), .out_9(s28), .in_5(main_27_out_10), .in_4(in_6));  // open: in_3, out_10
  strzal_2_main main_29 (
    .in_1(shift_register_2_q0), .in_2(shift_register_2_q1), .in_3(shift_register_2_q2),
    .in_4(shift_register_2_q3), .in_5(shift_register_2_q4), .in_6(shift_register_2_q5),
    .in_7(shift_register_2_q6), .in_8(shift_register_2_q7), .in_9(shift_register_2_q8),
    .in_10(shift_register_2_q9), .in_11(shift_register_2_q10), .in_12(shift_register_2_q11),
    .in_13(shift_register_2_q12), .in_14(shift_register_2_q13), .in_15(shift_register_2_q14),
    .in_16(shift_register_2_q15), .in_17(shift_register_2_q16), .in_18(shift_register_2_q17),
    .in_19(shift_register_2_q18), .in_20(shift_register_2_q19), .in_21(shift_register_2_q20),
    .in_22(shift_register_2_q21), .in_23(shift_register_2_q22), .in_24(shift_register_2_q23),
    .in_25(shift_register_2_q24), .in_26(shift_register_2_q25), .in_27(shift_register_2_q26),
    .in_28(shift_register_2_q27), .out_57(main_29_out_57), .out_58(main_29_out_58), .out_59(main_29_out_59),
    .out_60(main_29_out_60), .out_61(main_29_out_61), .out_62(main_29_out_62), .out_63(main_29_out_63),
    .out_64(main_29_out_64), .out_65(main_29_out_65), .out_66(main_29_out_66), .out_67(main_29_out_67),
    .out_68(main_29_out_68), .out_69(main_29_out_69), .out_70(main_29_out_70), .out_71(main_29_out_71),
    .out_72(main_29_out_72), .out_73(main_29_out_73), .out_74(main_29_out_74), .out_75(main_29_out_75),
    .out_76(main_29_out_76), .out_77(main_29_out_77), .out_78(main_29_out_78), .out_79(main_29_out_79),
    .out_80(main_29_out_80), .out_81(main_29_out_81), .out_82(main_29_out_82), .out_83(main_29_out_83),
    .in_29(s1), .in_30(s2), .in_31(s3), .in_32(s4), .in_33(s5), .in_34(s6), .in_35(s7), .in_36(s8),
    .in_37(s9), .in_38(s10), .in_39(s11), .in_40(s12), .in_41(s13), .in_42(s14), .in_43(s15), .in_44(s16),
    .in_45(s17), .in_46(s18), .in_47(s19), .in_48(s20), .in_49(s21), .in_50(s22), .in_51(s23), .in_52(s24),
    .in_53(s25), .in_54(s26), .in_55(s27), .in_56(s28));  // open: out_84
  or or_1 (out_15, main_1_out_8, main_2_out_8, main_3_out_8, main_4_out_8, main_5_out_8, main_6_out_8, main_7_out_8, main_8_out_8, main_9_out_8, main_10_out_8, main_11_out_8, main_12_out_8, main_13_out_8, main_14_out_8, main_15_out_8, main_16_out_8, main_17_out_8, main_18_out_8, main_19_out_8, main_20_out_8, main_21_out_8, main_22_out_8, main_23_out_8, main_24_out_8, main_25_out_8, main_26_out_8, main_27_out_8, main_28_out_8);
  or or_2 (out_7, s1, s2, s3, s4, s5, s6, s7, s8, s9, s10, s11, s12, s13, s14, s15, s16, s17, s18, s19, s20, s21, s22, s23, s24, s25, s26, s27, s28);

  // Other names for the same wires on the sheet: kol_a = out_15; kol_s = out_7
endmodule
