// Logisim project kolizja.circ as structural Verilog: 1 circuit, main circuit main
module main (
  input  [15:0] in_1,
  input  [15:0] in_2,
  input  [15:0] in_3,
  input  in_4,
  input  in_5,
  output [15:0] out_6,
  output [15:0] out_7,
  output out_8,
  output out_9,
  output out_10
);

  wire comparator_1_gt, comparator_2_gt, comparator_3_gt, register_2_q;
  wire [15:0] and_1_out, and_2_out, multiplexer_1_out, xor_1_out, xor_2_out;

  assign and_1_out = in_1 & in_3;  // AND_Gate and_1, 16 bits wide
  assign xor_1_out = in_1 ^ in_2;  // XOR_Gate xor_1, 16 bits wide
  assign and_2_out = in_1 & in_2;  // AND_Gate and_2, 16 bits wide
  Multiplexer #(.width(16), .disabled(0), .enable("false")) multiplexer_1 (
    .in0(in_1), .in1(xor_1_out), .out(multiplexer_1_out), .sel(out_8));
  assign xor_2_out = in_1 ^ in_3;  // XOR_Gate xor_2, 16 bits wide
  Comparator #(.width(16), .mode("unsigned")) comparator_1 (
    .a(and_2_out), .b({16{1'b0}}), .gt(comparator_1_gt));  // open: eq, lt
  Comparator #(.width(16), .mode("unsigned")) comparator_2 (
    .a(and_2_out), .b({16{1'b0}}), .gt(comparator_2_gt));  // open: eq, lt
  Comparator #(.width(16), .mode("unsigned")) comparator_3 (
    .a(and_1_out), .b({16{1'b0}}), .gt(comparator_3_gt));  // open: eq, lt
  Multiplexer #(.width(16), .disabled(0), .enable("false")) multiplexer_2 (
    .in0(multiplexer_1_out), .in1(xor_2_out), .out(out_7), .sel(out_10));
  Register #(.width(1), .trigger("falling")) register_1 (.D(comparator_3_gt), .Q(out_10), .clk(in_4));  // open: en, clr
  Register #(.width(1), .trigger("low")) register_2 (.D(in_5), .Q(register_2_q), .clk(in_4));  // open: en, clr
  assign out_6 = out_7 | in_2;  // OR_Gate or_1, 16 bits wide
  Multiplexer #(.disabled(0), .enable("false")) multiplexer_3 (
    .in0(comparator_1_gt), .in1(1'b1), .out(out_8), .sel(out_10));
  Multiplexer #(.disabled(0), .enable("false")) multiplexer_4 (
    .in0(comparator_2_gt), .in1(1'b1), .out(out_9), .sel(register_2_q));
endmodule
