// Logisim project strzal_2.circ as structural Verilog: 1 circuit, main circuit main
module main (
  input  [15:0] in_1,
  input  [15:0] in_2,
  input  [15:0] in_3,
  input  [15:0] in_4,
  input  [15:0] in_5,
  input  [15:0] in_6,
  input  [15:0] in_7,
  input  [15:0] in_8,
  input  [15:0] in_9,
  input  [15:0] in_10,
  input  [15:0] in_11,
  input  [15:0] in_12,
  input  [15:0] in_13,
  input  [15:0] in_14,
  input  [15:0] in_15,
  input  [15:0] in_16,
  input  [15:0] in_17,
  input  [15:0] in_18,
  input  [15:0] in_19,
  input  [15:0] in_20,
  input  [15:0] in_21,
  input  [15:0] in_22,
  input  [15:0] in_23,
  input  [15:0] in_24,
  input  [15:0] in_25,
  input  [15:0] in_26,
  input  [15:0] in_27,
  input  [15:0] in_28,
  input  in_29,
  input  in_30,
  input  in_31,
  input  in_32,
  input  in_33,
  input  in_34,
  input  in_35,
  input  in_36,
  input  in_37,
  input  in_38,
  input  in_39,
  input  in_40,
  input  in_41,
  input  in_42,
  input  in_43,
  input  in_44,
  input  in_45,
  input  in_46,
  input  in_47,
  input  in_48,
  input  in_49,
  input  in_50,
  input  in_51,
  input  in_52,
  input  in_53,
  input  in_54,
  input  in_55,
  input  in_56,
  output [15:0] out_57,
  output [15:0] out_58,
  output [15:0] out_59,
  output [15:0] out_60,
  output [15:0] out_61,
  output [15:0] out_62,
  output [15:0] out_63,
  output [15:0] out_64,
  output [15:0] out_65,
  output [15:0] out_66,
  output [15:0] out_67,
  output [15:0] out_68,
  output [15:0] out_69,
  output [15:0] out_70,
  output [15:0] out_71,
  output [15:0] out_72,
  output [15:0] out_73,
  output [15:0] out_74,
  output [15:0] out_75,
  output [15:0] out_76,
  output [15:0] out_77,
  output [15:0] out_78,
  output [15:0] out_79,
  output [15:0] out_80,
  output [15:0] out_81,
  output [15:0] out_82,
  output [15:0] out_83,
  output [15:0] out_84
);

  wire not_1_out, not_2_out, not_3_out, not_4_out, not_5_out, not_6_out, not_7_out, not_8_out, not_9_out,
       not_10_out, not_11_out, not_12_out, not_13_out, not_14_out, not_15_out, not_16_out, not_17_out,
       not_18_out, not_19_out, not_20_out, not_21_out, not_22_out, not_23_out, not_24_out, not_25_out,
       not_26_out, not_27_out, not_28_out;

  assign out_57 = not_1_out ? in_1 : 16'bz;  // Controlled_Buffer controlled_buffer_1
  assign out_58 = not_4_out ? in_2 : 16'bz;  // Controlled_Buffer controlled_buffer_2
  assign out_59 = not_3_out ? in_3 : 16'bz;  // Controlled_Buffer controlled_buffer_3
  not not_1 (not_1_out, in_29);
  not not_2 (not_2_out, in_32);
  not not_3 (not_3_out, in_31);
  not not_4 (not_4_out, in_30);
  assign out_60 = not_2_out ? in_4 : 16'bz;  // Controlled_Buffer controlled_buffer_4
  assign out_61 = not_7_out ? in_5 : 16'bz;  // Controlled_Buffer controlled_buffer_5
  assign out_62 = not_5_out ? in_6 : 16'bz;  // Controlled_Buffer controlled_buffer_6
  assign out_63 = not_8_out ? in_7 : 16'bz;  // Controlled_Buffer controlled_buffer_7
  not not_5 (not_5_out, in_34);
  not not_6 (not_6_out, in_36);
  not not_7 (not_7_out, in_33);
  not not_8 (not_8_out, in_35);
  assign out_64 = not_6_out ? in_8 : 16'bz;  // Controlled_Buffer controlled_buffer_8
  assign out_65 = not_11_out ? in_9 : 16'bz;  // Controlled_Buffer controlled_buffer_9
  assign out_66 = not_9_out ? in_10 : 16'bz;  // Controlled_Buffer controlled_buffer_10
  assign out_67 = not_12_out ? in_11 : 16'bz;  // Controlled_Buffer controlled_buffer_11
  not not_9 (not_9_out, in_38);
  not not_10 (not_10_out, in_40);
  not not_11 (not_11_out, in_37);
  not not_12 (not_12_out, in_39);
  assign out_68 = not_10_out ? in_12 : 16'bz;  // Controlled_Buffer controlled_buffer_12
  assign out_69 = not_14_out ? in_13 : 16'bz;  // Controlled_Buffer controlled_buffer_13
  assign out_70 = not_13_out ? in_14 : 16'bz;  // Controlled_Buffer controlled_buffer_14
  assign out_71 = not_15_out ? in_15 : 16'bz;  // Controlled_Buffer controlled_buffer_15
  not not_13 (not_13_out, in_42);
  not not_14 (not_14_out, in_41);
  not not_15 (not_15_out, in_43);
  not not_16 (not_16_out, in_44);
  assign out_72 = not_16_out ? in_16 : 16'bz;  // Controlled_Buffer controlled_buffer_16
  assign out_73 = not_19_out ? in_17 : 16'bz;  // Controlled_Buffer controlled_buffer_17
  assign out_74 = not_20_out ? in_18 : 16'bz;  // Controlled_Buffer controlled_buffer_18
  assign out_75 = not_18_out ? in_19 : 16'bz;  // Controlled_Buffer controlled_buffer_19
  not not_17 (not_17_out, in_48);
  not not_18 (not_18_out, in_47);
  not not_19 (not_19_out, in_45);
  not not_20 (not_20_out, in_46);
  assign out_76 = not_17_out ? in_20 : 16'bz;  // Controlled_Buffer controlled_buffer_20
  assign out_77 = not_21_out ? in_21 : 16'bz;  // Controlled_Buffer controlled_buffer_21
  assign out_78 = not_23_out ? in_22 : 16'bz;  // Controlled_Buffer controlled_buffer_22
  assign out_79 = not_24_out ? in_23 : 16'bz;  // Controlled_Buffer controlled_buffer_23
  not not_21 (not_21_out, in_49);
  not not_22 (not_22_out, in_52);
  not not_23 (not_23_out, in_50);
  not not_24 (not_24_out, in_51);
  assign out_80 = not_22_out ? in_24 : 16'bz;  // Controlled_Buffer controlled_buffer_24
  assign out_81 = not_26_out ? in_25 : 16'bz;  // Controlled_Buffer controlled_buffer_25
  assign out_82 = not_27_out ? in_26 : 16'bz;  // Controlled_Buffer controlled_buffer_26
  assign out_83 = not_28_out ? in_27 : 16'bz;  // Controlled_Buffer controlled_buffer_27
  not not_25 (not_25_out, in_56);
  not not_26 (not_26_out, in_53);
  not not_27 (not_27_out, in_54);
  not not_28 (not_28_out, in_55);
  Pull_Resistor pull_resistor_1 (.node(out_57));
  Pull_Resistor pull_resistor_2 (.node(out_58));
  Pull_Resistor pull_resistor_3 (.node(out_59));
  Pull_Resistor pull_resistor_4 (.node(out_60));
  Pull_Resistor pull_resistor_5 (.node(out_61));
  Pull_Resistor pull_resistor_6 (.node(out_62));
  Pull_Resistor pull_resistor_7 (.node(out_63));
  Pull_Resistor pull_resistor_8 (.node(out_64));
  Pull_Resistor pull_resistor_9 (.node(out_65));
  Pull_Resistor pull_resistor_10 (.node(out_66));
  Pull_Resistor pull_resistor_11 (.node(out_67));
  Pull_Resistor pull_resistor_12 (.node(out_68));
  Pull_Resistor pull_resistor_13 (.node(out_69));
  Pull_Resistor pull_resistor_14 (.node(out_70));
  Pull_Resistor pull_resistor_15 (.node(out_71));
  Pull_Resistor pull_resistor_16 (.node(out_72));
  Pull_Resistor pull_resistor_17 (.node(out_73));
  Pull_Resistor pull_resistor_18 (.node(out_74));
  Pull_Resistor pull_resistor_19 (.node(out_75));
  Pull_Resistor pull_resistor_20 (.node(out_76));
  Pull_Resistor pull_resistor_21 (.node(out_77));
  Pull_Resistor pull_resistor_22 (.node(out_78));
  Pull_Resistor pull_resistor_23 (.node(out_79));
  Pull_Resistor pull_resistor_24 (.node(out_80));
  Pull_Resistor pull_resistor_25 (.node(out_81));
  Pull_Resistor pull_resistor_26 (.node(out_82));
  Pull_Resistor pull_resistor_27 (.node(out_83));
  Pull_Resistor pull_resistor_28 (.node(out_84));
  assign out_84 = not_25_out ? in_28 : 16'bz;  // Controlled_Buffer controlled_buffer_28
endmodule
